# Fritzing sketch Ampoule READ (saved by Fritzing 1.0.6)
circuit board: 2.38269cm x 2.28914cm

parts:
  J1 = female pin header, 3 pins [form="♀ (female)"]
  J2 = female pin header, 4 pins [form="♀ (female)"]
  J3 = female pin header, 1 pin [form="♀ (female)"]
  J4 = female pin header, 1 pin [form="♀ (female)"]

nets:
  N1: J1.pin1, J2.pin1
  N2: J1.pin2, J2.pin2, J3.pin1
  N3: J1.pin3, J2.pin3
  N4: J2.pin4, J4.pin1
