# Fritzing sketch ESP Barriere (saved by Fritzing 1.0.6)
circuit board: 6.49084cm x 5.23314cm

parts:
  ESP32-WROOM-32 = MH-ET LIVE ESP32 DEVKIT 38 pins
  Servo = female pin header, 3 pins [form="♀ (female)"]
  LED_RFID = female pin header, 3 pins [form="♀ (female)"]
  HC-SR04 = female pin header, 4 pins [form="♀ (female)"]
  RFID = female pin header, 7 pins [form="♀ (female)"]

nets:
  N1: ESP32-WROOM-32.RST, RFID.pin6
  N2: ESP32-WROOM-32.SVP, RFID.pin5
  N3: ESP32-WROOM-32.IO35, RFID.pin4
  N4: ESP32-WROOM-32.IO32, RFID.pin3
  N5: ESP32-WROOM-32.IO33, RFID.pin2
  N6: ESP32-WROOM-32.IO25, RFID.pin1
  N7: ESP32-WROOM-32.GND#64, HC-SR04.pin4, RFID.pin7
  N8: ESP32-WROOM-32.GND#70, HC-SR04.pin2
  N9: ESP32-WROOM-32.IO19, HC-SR04.pin1
  N10: ESP32-WROOM-32.IO18, LED_RFID.pin3
  N11: ESP32-WROOM-32.IO5, LED_RFID.pin1
  N12: ESP32-WROOM-32.IO0, Servo.pin3, LED_RFID.pin2, HC-SR04.pin3
  N13: ESP32-WROOM-32.IO2, Servo.pin1
  N14: ESP32-WROOM-32.SCK, Servo.pin2

custom parts:
  MH-ET LIVE ESP32 DEVKIT 38 pins: http://mh.nodebb.com/topic/2/mh-et-live-esp32-devkit
