# Fritzing sketch ESP Parking (saved by Fritzing 1.0.6)
circuit board: 6.94318cm x 5.27869cm

parts:
  Heltec_WiFi_LoRa_32_V1 = Heltec WiFi LoRa 32 V2 [part_number=HTIT-WB32LA]
  IR = female pin header, 6 pins [form="♀ (female)"]
  Hall = female pin header, 5 pins [form="♀ (female)"]
  READ = female pin header, 4 pins [form="♀ (female)"]

nets:
  N1: Heltec_WiFi_LoRa_32_V1.pin_1, IR.pin5
  N2: Heltec_WiFi_LoRa_32_V1.pin_2, IR.pin6
  N3: Heltec_WiFi_LoRa_32_V1.pin_3, READ.pin2
  N4: Heltec_WiFi_LoRa_32_V1.pin_7, READ.pin3
  N5: Heltec_WiFi_LoRa_32_V1.pin_9, IR.pin3
  N6: Heltec_WiFi_LoRa_32_V1.pin_16, IR.pin2, Hall.pin2
  N7: Heltec_WiFi_LoRa_32_V1.pin_18, Heltec_WiFi_LoRa_32_V1.pin_19, IR.pin1, Hall.pin1, READ.pin4
  N8: Heltec_WiFi_LoRa_32_V1.pin_27, Hall.pin3
  N9: Heltec_WiFi_LoRa_32_V1.pin_29, Hall.pin5
  N10: Heltec_WiFi_LoRa_32_V1.pin_33, Hall.pin4
  N11: Heltec_WiFi_LoRa_32_V1.pin_35, READ.pin1

custom parts:
  Heltec WiFi LoRa 32 V2: Heltec WiFi LoRa 32 V2 WiFi LoRa 32 is a classic IoT dev-board designed & produced by Heltec Automation(TM). It’s a highly integrated product based on ESP32 + SX127x, it has Wi-Fi, BLE, LoRa functions, also Li-Po battery management system, 0.96″ OLED are also included. It’s the best choice for smart cities, smart farms, smart home, and IoT makers.
