# Fritzing sketch Hall (saved by Fritzing 1.0.6)
circuit board: 2.68773cm x 2.01167cm

parts:
  J1 = female pin header, 3 pins [form="♀ (female)"]
  J3 = female pin header, 3 pins [form="♀ (female)"]
  J2 = female pin header, 5 pins [form="♀ (female)"]

nets:
  N1: J1.pin1, J2.pin3
  N2: J1.pin2, J3.pin3, J2.pin4
  N3: J1.pin3, J2.pin5
  N4: J3.pin1, J2.pin2
  N5: J3.pin2, J2.pin1
