# Fritzing sketch LEDs RFID (saved by Fritzing 1.0.6)
circuit board: 3.5cm x 1.5cm

parts:
  J2 = female pin header, 2 pins [form="♀ (female)"]
  J3 = female pin header, 2 pins [form="♀ (female)"]
  R1 = Resistor [tolerance=±5% power=0.25W resistance=220 package=THT]
  R2 = Resistor [tolerance=±5% power=0.25W resistance=220 package=THT]
  J4 = female pin header, 3 pins [form="♀ (female)"]

nets:
  N1: J2.pin1, J3.pin2, J4.pin2
  N2: J2.pin2, R2.Pin_1
  N3: J3.pin1, R1.Pin_1
  N4: R1.Pin_0, J4.pin1
  N5: R2.Pin_0, J4.pin3
