# Fritzing sketch LEDs parking (saved by Fritzing 1.0.6)
circuit board: 2.62907cm x 2.89042cm

parts:
  LED1 = LED - 5mm [color="Red (633nm)" current=0.030A package="5 mm [THT]"]
  LED2 = LED - 5mm [color="Green (565nm)" current=0.030A package="5 mm [THT]"]
  J1 = female pin header, 3 pins [form="♀ (female)"]
  R1 = Resistor [tolerance=±5% power=0.25W resistance=220 package=THT]
  R2 = Resistor [tolerance=±5% power=0.25W resistance=220 package=THT]

nets:
  N1: LED1.cathode, LED2.cathode, J1.pin2
  N2: LED1.anode, R1.Pin_0
  N3: LED2.anode, R2.Pin_0
  N4: J1.pin1, R2.Pin_1
  N5: J1.pin3, R1.Pin_1
